# Fritzing sketch xmas_tree (saved by Fritzing 0.8.0b)
breadboards: 1

parts:
  Componente1 = Arduino Uno (Rev3)
  R1 = Resistor [tolerance=±5% resistance=68 package=THT]
  J1 = Infrared Proximity Sensor
  LED1 = LED - 5mm [color="Red (633nm)" package="5 mm [THT]"]
  LED2 = LED - 5mm [color="Yellow (595nm)" package="5 mm [THT]"]
  LED3 = LED - 5mm [color="Green (565nm)" package="5 mm [THT]"]
  R4 = Resistor [tolerance=±5% resistance=68 package=THT]
  R5 = Resistor [tolerance=±5% resistance=68 package=THT]

nets:
  N1: Componente1.A0, J1.Vout
  GND: Componente1.GND, R1.Pin_1, J1.GND, R4.Pin_1, R5.Pin_1
  N2: Componente1.D9_PWM, LED3.anode
  N3: Componente1.D10_PWM/SS, LED2.anode
  N4: Componente1.D11_PWM/MOSI, LED1.anode
  5V: Componente1.5V, J1.Vcc
  N5: R1.Pin_0, LED1.cathode
  N6: LED2.cathode, R4.Pin_0
  N7: LED3.cathode, R5.Pin_0
